# Fritzing sketch schematics_electric-diagram (saved by Fritzing 0.9.3b)
perfboards: 1

parts:
  Part2 = Arduino Uno (Rev3) - ICSP
  LED5 = smd LED [color="Orange (620nm)" package="0805 [SMD]"]  # not connected
  LED8 = smd LED [color="Yellow (585nm)" package="0805 [SMD]"]
  R2 = Resistor [tolerance=±5% resistance=100 package=THT]
  R4 = Resistor [tolerance=±5% resistance=100 package=THT]
  R5 = Resistor [tolerance=±5% resistance=47 package=THT]
  R6 = Resistor [tolerance=±5% resistance=39 package=THT]
  LED9 = smd LED [color="White (6500K)" package="0805 [SMD]"]
  LED10 = smd LED [color="White (6500K)" package="0805 [SMD]"]  # not connected
  LED11 = smd LED [color="Red (633nm)" package="0805 [SMD]"]
  LED12 = smd LED [color="Red (633nm)" package="0805 [SMD]"]
  LED13 = smd LED [color="Green (555nm)" package="0805 [SMD]"]
  LED14 = smd LED [color="Green (555nm)" package="0805 [SMD]"]
  LED15 = smd LED [color="Yellow (585nm)" package="0805 [SMD]"]
  LED16 = smd LED [color="Yellow (585nm)" package="0805 [SMD]"]
  LED17 = smd LED [color="Yellow (585nm)" package="0805 [SMD]"]
  R7 = Resistor [tolerance=±5% resistance=68 package=THT]
  R8 = Resistor [tolerance=±5% resistance=68 package=THT]
  LED18 = smd LED [color="Orange (620nm)" package="0805 [SMD]"]
  LED19 = smd LED [color="Blue (430nm)" package="0805 [SMD]"]
  LED20 = smd LED [color="Blue (430nm)" package="0805 [SMD]"]
  R9 = Resistor [tolerance=±5% resistance=22 package=THT]
  Part3 = Photon
  LCD1 = LCD screen  # not connected

nets:
  N1: Part2.ICSP_MOSI, Part2.D11_PWM/MOSI, R4.Pin_1
  N2: Part2.D9_PWM, R5.Pin_0
  N3: Part2.D10_PWM/SS, R6.Pin_0
  N4: Part2.D12/MISO, R2.Pin_1
  N5: Part2.D13/SCK, Part3.D4
  N6: Part2.D2, Part3.D3
  N7: Part2.D3_PWM, R7.Pin_1
  N8: Part2.D4, Part3.D2
  N9: Part2.D5_PWM, R8.Pin_1
  N10: Part2.D6_PWM, R9.Pin_0
  N11: Part2.D7, Part3.D1
  N12: LED8.cathode, LED11.cathode
  N13: R2.Pin_0, LED14.anode
  N14: R4.Pin_0, LED12.anode
  N15: R5.Pin_1, LED18.anode
  N16: R6.Pin_1, LED19.anode, LED20.anode
  N17: LED9.anode, R9.Pin_1
  N18: LED11.anode, LED12.cathode
  N19: LED13.cathode, LED15.cathode, LED17.cathode
  N20: LED13.anode, LED14.cathode
  N21: LED15.anode, R7.Pin_0
  N22: LED16.anode, R8.Pin_0

notes:
  Particle CORE as interface with Alexa, connected devices, local network/internet...
  State Information signals
  (cyan wires)
  Ilumination Prototype Board
  to represent all the ilumination transitions and Weather/Traffic Information states
  LCD screen for debugging purposes (connected through SDL/SCL pins on the DF Robot I/O Expansion Shield)
